# Fritzing sketch 7seg (saved by Fritzing 1.0.0rc)
breadboards: 1

parts:
  Mod1 = Raspberry Pi Pico W
  7_Segment1 = 7 Segment Display

nets:
  N1: Mod1.pin_3, Mod1.pin_8, Mod1.pin_13, Mod1.pin_18, Mod1.pin_23, Mod1.pin_28, Mod1.pin_33, Mod1.pin_38
  N2: Mod1.pin_4, 7_Segment1.Segment_A
  N3: Mod1.pin_5, 7_Segment1.Segment_B
  N4: Mod1.pin_6, 7_Segment1.Segment_C
  N5: Mod1.pin_7, 7_Segment1.Segment_D
  N6: Mod1.pin_9, 7_Segment1.Segment_E
  N7: Mod1.pin_10, 7_Segment1.Segment_G
  N8: Mod1.pin_11, 7_Segment1.Segment_F
  N9: Mod1.pin_12, 7_Segment1.Segment_DP
  N10: Mod1.pin_36, 7_Segment1.common_cathode

custom parts:
  Raspberry Pi Pico W: Raspberry Pi Pico W. Based around the RP2040 microcontroller the Pico W is a low cost microcontroller device bringing Raspberry Pi quality, cost, and easy of use to the microcontroller space. The areas marked KEEPOUT in pcb silkscreen should not have traces running through them to avoid shorts on a soldered in module!
